# Fritzing sketch 电路 (saved by Fritzing 0.9.3b)
breadboards: 1

parts:
  元件1 = Arduino Uno (Rev3)
  LED1 = RGB LED (com. cathode, rgb) [package="5 mm [THT]"]
  R1 = Resistor [tolerance=±5% resistance=220 package=THT]
  R2 = Resistor [tolerance=±5% resistance=220 package=THT]
  R3 = Resistor [tolerance=±5% resistance=220 package=THT]
  hc-sr1 = hc-sr04
  S1 = Pushbutton [package="[THT]"]
  R4 = Resistor [tolerance=±5% resistance=220 package=THT]
  LED2 = LED - 5mm [color="Red (633nm)" package="5 mm [THT]"]
  R5 = Resistor [tolerance=±5% resistance=220 package=THT]

nets:
  N1: 元件1.D10_PWM/SS, hc-sr1.Echo
  N2: 元件1.D11_PWM/MOSI, hc-sr1.Trig
  N3: 元件1.D2, R5.Pin_1
  N4: 元件1.D3_PWM, R1.Pin_0
  N5: 元件1.D5_PWM, R2.Pin_0
  N6: 元件1.D6_PWM, R3.Pin_0
  N7: 元件1.D7, S1.Pin_1, S1.Pin_2, R4.Pin_0
  5V: 元件1.5V, hc-sr1.VCC, S1.Pin_3, S1.Pin_4
  GND: 元件1.GND, LED1.common_cathode, hc-sr1.GND, R4.Pin_1, LED2.anode
  N8: LED1.red_anode, R3.Pin_1
  N9: LED1.green_anode, R2.Pin_1
  N10: LED1.blue_anode, R1.Pin_1
  N11: LED2.cathode, R5.Pin_0
